// Digital circuit core.dig as structural Verilog
module core (
  input  [31:0] k1,
  input  [31:0] k2,
  input  [31:0] k3,
  input  [31:0] k4,
  input  [31:0] k5,
  input  [31:0] k6,
  input  [31:0] k7,
  input  [31:0] k0,
  input  [31:0] n0,
  input  [31:0] n1,
  input  [31:0] n2,
  input  rst,
  input  start,
  input  [31:0] counter0,
  input  [31:0] in__data,
  input  in__valid,
  input  in__last,
  input  [3:0] in__keep,
  input  CLK,
  input  out__ready,
  output [31:0] out__data,
  output out__valid,
  output out__last,
  output [3:0] out__keep,
  output in__ready
);

  wire acc, avail, bstart, capd, capgen, capx, cb, done, genacc, hs, ks__capture, load, navail, ncb, nlast,
       or_1_out, or_2_out, rdy, rdyn, st__gen, st__idle, st__xor, w15, w15gen, w__inc, wrap, wrapn;
  wire [3:0] add_2_s, multiplexer_1_out, w;
  wire [31:0] add_1_s, bc, bcblk, ks__word, kwx, multiplexer_2_out, o0, o1, o2, o3, o4, o5, o6, o7, o8, o9,
       o10, o11, o12, o13, o14, o15, ow, register_1_q, register_2_q, register_3_q, register_4_q,
       register_7_q, register_8_q, register_9_q, register_10_q, register_11_q, register_12_q, register_13_q,
       register_14_q, register_15_q, register_16_q, register_17_q, register_18_q;

  Add #(.Bits(32)) add_1 (.a(bc), .b(32'h1), .c_i(1'b0), .s(add_1_s));  // open: c_o
  Add #(.Bits(4)) add_2 (.a(w), .b(4'b0001), .c_i(1'b0), .s(add_2_s));  // open: c_o
  Register #(.Bits(32)) register_1 (.D(o0), .C(CLK), .en(ks__capture), .Q(register_1_q));
  Register #(.Bits(32)) register_2 (.D(o1), .C(CLK), .en(ks__capture), .Q(register_2_q));
  Multiplexer #(.Bits(4)) multiplexer_1 (.sel(w__inc), .in_0(4'b0000), .in_1(add_2_s), .out(multiplexer_1_out));
  or or_1 (or_1_out, load, w__inc);
  Register #(.Bits(32)) register_3 (.D(o2), .C(CLK), .en(ks__capture), .Q(register_3_q));
  Multiplexer #(.Bits(32)) multiplexer_2 (.sel(ks__capture), .in_0(counter0), .in_1(add_1_s), .out(multiplexer_2_out));
  or or_2 (or_2_out, load, ks__capture);
  Register #(.Bits(32)) register_4 (.D(o3), .C(CLK), .en(ks__capture), .Q(register_4_q));
  Register #(.Bits(32)) register_5 (.D(multiplexer_2_out), .C(CLK), .en(or_2_out), .Q(bc));
  Register #(.Bits(4)) register_6 (.D(multiplexer_1_out), .C(CLK), .en(or_1_out), .Q(w));
  and and_1 (w15, w[0], w[1], w[2], w[3]);
  Register #(.Bits(32)) register_7 (.D(o4), .C(CLK), .en(ks__capture), .Q(register_7_q));
  ctrl ctrl_1 (
    .done(avail), .hs(hs), .last(in__last), .start(start), .w15(w15gen), .C(CLK), .rst(rst),
    .st_gen(st__gen), .st_idle(st__idle), .st_xor(st__xor));
  Register #(.Bits(32)) register_8 (.D(o5), .C(CLK), .en(ks__capture), .Q(register_8_q));
  block_function block_function_1 (
    .k0(k0), .k1(k1), .k2(k2), .k3(k3), .k4(k4), .k5(k5), .k6(k6), .k7(k7), .bc(bcblk), .n0(n0), .n1(n1),
    .n2(n2), .start(bstart), .clk(CLK), .o0(o0), .o1(o1), .o2(o2), .o3(o3), .o4(o4), .o5(o5), .o6(o6),
    .o7(o7), .o8(o8), .o9(o9), .o10(o10), .o11(o11), .o12(o12), .o13(o13), .o14(o14), .o15(o15), .done(done));
  Register #(.Bits(32)) register_9 (.D(o6), .C(CLK), .en(ks__capture), .Q(register_9_q));
  Register #(.Bits(32)) register_10 (.D(o7), .C(CLK), .en(ks__capture), .Q(register_10_q));
  Register #(.Bits(32)) register_11 (.D(o8), .C(CLK), .en(ks__capture), .Q(register_11_q));
  Register #(.Bits(32)) register_12 (.D(o9), .C(CLK), .en(ks__capture), .Q(register_12_q));
  and and_2 (in__ready, acc, out__ready);
  and and_3 (out__valid, acc, in__valid);
  and and_4 (hs, in__valid, in__ready);
  and and_5 (load, st__idle, start);
  Register #(.Bits(32)) register_13 (.D(o10), .C(CLK), .en(ks__capture), .Q(register_13_q));
  Register #(.Bits(32)) register_14 (.D(o11), .C(CLK), .en(ks__capture), .Q(register_14_q));
  Register #(.Bits(32)) register_15 (.D(o12), .C(CLK), .en(ks__capture), .Q(register_15_q));
  assign out__data = in__data ^ kwx;  // XOr xor_1, 32 bits wide
  Register #(.Bits(32)) register_16 (.D(o13), .C(CLK), .en(ks__capture), .Q(register_16_q));
  and and_6 (capgen, st__gen, avail);
  and and_7 (w__inc, acc, hs);
  and and_8 (wrap, hs, st__xor, w15);
  Register #(.Bits(32)) register_17 (.D(o14), .C(CLK), .en(ks__capture), .Q(register_17_q));
  Register #(.Bits(32)) register_18 (.D(o15), .C(CLK), .en(ks__capture), .Q(register_18_q));
  Multiplexer #(.Selector_Bits(4), .Bits(32)) multiplexer_3 (
    .sel(w), .in_0(register_1_q), .in_1(register_2_q), .in_2(register_3_q), .in_3(register_4_q),
    .in_4(register_7_q), .in_5(register_8_q), .in_6(register_9_q), .in_7(register_10_q),
    .in_8(register_11_q), .in_9(register_12_q), .in_10(register_13_q), .in_11(register_14_q),
    .in_12(register_15_q), .in_13(register_16_q), .in_14(register_17_q), .in_15(register_18_q), .out(ks__word));
  or or_3 (avail, done, rdy);
  not not_1 (navail, avail);
  and and_9 (w15gen, w15, navail);
  not not_2 (nlast, in__last);
  and and_10 (wrapn, wrap, nlast);
  and and_11 (capx, wrapn, avail);
  or or_4 (ks__capture, capgen, capx);
  D_FF u_capd (.D(ks__capture), .C(CLK), .Q(capd));  // open: nQ
  or or_5 (bstart, load, capd);
  Multiplexer #(.Bits(32)) multiplexer_4 (.sel(st__idle), .in_0(bc), .in_1(counter0), .out(bcblk));
  or or_6 (cb, ks__capture, bstart);
  not not_3 (ncb, cb);
  and and_12 (rdyn, avail, ncb);
  D_FF u_rdy (.D(rdyn), .C(CLK), .Q(rdy));  // open: nQ
  and and_13 (genacc, st__gen, avail);
  or or_7 (acc, st__xor, genacc);
  Multiplexer #(.Bits(32), .Selector_Bits(4)) multiplexer_5 (
    .sel(w), .in_0(o0), .in_1(o1), .in_2(o2), .in_3(o3), .in_4(o4), .in_5(o5), .in_6(o6), .in_7(o7),
    .in_8(o8), .in_9(o9), .in_10(o10), .in_11(o11), .in_12(o12), .in_13(o13), .in_14(o14), .in_15(o15),
    .out(ow));
  Multiplexer #(.Bits(32)) multiplexer_6 (.sel(st__gen), .in_0(ks__word), .in_1(ow), .out(kwx));

  assign out__keep = in__keep;
  assign out__last = in__last;

  // Notes on the sheet:
  //   Encryption Algorithm
  //   Block Counter
  //   Word Counter
  //   Keystream Register
  //   State Machine
  //   Glue Logic
  //   Data XOR
  //   Pass-throughts
  //   Inputs
  //   Outputs
  //   Block Prefetch
  //   First Word Bypass
endmodule

/* Test case test0:
rst CLK start counter0 in\_valid in\_last in\_keep out\_ready in\_data k0 k1 k2 k3 k4 k5 k6 k7 n0 n1 n2   out\_data out\_valid out\_last out\_keep in\_ready

# reset, then start (IDLE -> GEN -> XOR)
1 C 0 1 0 0 0 1 0 0x03020100 0x07060504 0x0b0a0908 0x0f0e0d0c 0x13121110 0x17161514 0x1b1a1918 0x1f1e1d1c 0x00000000 0x4a000000 0x00000000   X X X X X
0 C 1 1 0 0 0 1 0 0x03020100 0x07060504 0x0b0a0908 0x0f0e0d0c 0x13121110 0x17161514 0x1b1a1918 0x1f1e1d1c 0x00000000 0x4a000000 0x00000000   X X X X 0
# GEN: 9 more clocks while the block computes; after the last one the keystream is ready
0 C 0 1 0 0 0 1 0 0x03020100 0x07060504 0x0b0a0908 0x0f0e0d0c 0x13121110 0x17161514 0x1b1a1918 0x1f1e1d1c 0x00000000 0x4a000000 0x00000000   X X X X 0
0 C 0 1 0 0 0 1 0 0x03020100 0x07060504 0x0b0a0908 0x0f0e0d0c 0x13121110 0x17161514 0x1b1a1918 0x1f1e1d1c 0x00000000 0x4a000000 0x00000000   X X X X 0
0 C 0 1 0 0 0 1 0 0x03020100 0x07060504 0x0b0a0908 0x0f0e0d0c 0x13121110 0x17161514 0x1b1a1918 0x1f1e1d1c 0x00000000 0x4a000000 0x00000000   X X X X 0
0 C 0 1 0 0 0 1 0 0x03020100 0x07060504 0x0b0a0908 0x0f0e0d0c 0x13121110 0x17161514 0x1b1a1918 0x1f1e1d1c 0x00000000 0x4a000000 0x00000000   X X X X 0
0 C 0 1 0 0 0 1 0 0x03020100 0x07060504 0x0b0a0908 0x0f0e0d0c 0x13121110 0x17161514 0x1b1a1918 0x1f1e1d1c 0x00000000 0x4a000000 0x00000000   X X X X 0
0 C 0 1 0 0 0 1 0 0x03020100 0x07060504 0x0b0a0908 0x0f0e0d0c 0x13121110 0x17161514 0x1b1a1918 0x1f1e1d1c 0x00000000 0x4a000000 0x00000000   X X X X 0
0 C 0 1 0 0 0 1 0 0x03020100 0x07060504 0x0b0a0908 0x0f0e0d0c 0x13121110 0x17161514 0x1b1a1918 0x1f1e1d1c 0x00000000 0x4a000000 0x00000000   X X X X 0
0 C 0 1 0 0 0 1 0 0x03020100 0x07060504 0x0b0a0908 0x0f0e0d0c 0x13121110 0x17161514 0x1b1a1918 0x1f1e1d1c 0x00000000 0x4a000000 0x00000000   X X X X 0
0 C 0 1 0 0 0 1 0 0x03020100 0x07060504 0x0b0a0908 0x0f0e0d0c 0x13121110 0x17161514 0x1b1a1918 0x1f1e1d1c 0x00000000 0x4a000000 0x00000000   X X X X 1
# word 0
0 0 0 1 1 0 15 1 0x6964614c 0x03020100 0x07060504 0x0b0a0908 0x0f0e0d0c 0x13121110 0x17161514 0x1b1a1918 0x1f1e1d1c 0x00000000 0x4a000000 0x00000000   0x9a352e6e 1 0 15 1
0 C 0 1 1 0 15 1 0x6964614c 0x03020100 0x07060504 0x0b0a0908 0x0f0e0d0c 0x13121110 0x17161514 0x1b1a1918 0x1f1e1d1c 0x00000000 0x4a000000 0x00000000   X X X X X
# word 1
0 0 0 1 1 0 15 1 0x61207365 0x03020100 0x07060504 0x0b0a0908 0x0f0e0d0c 0x13121110 0x17161514 0x1b1a1918 0x1f1e1d1c 0x00000000 0x4a000000 0x00000000   0x80f96825 1 0 15 1
0 C 0 1 1 0 15 1 0x61207365 0x03020100 0x07060504 0x0b0a0908 0x0f0e0d0c 0x13121110 0x17161514 0x1b1a1918 0x1f1e1d1c 0x00000000 0x4a000000 0x00000000   X X X X X
# word 2
0 0 0 1 1 0 15 1 0x4720646e 0x03020100 0x07060504 0x0b0a0908 0x0f0e0d0c 0x13121110 0x17161514 0x1b1a1918 0x1f1e1d1c 0x00000000 0x4a000000 0x00000000   0x2807ba41 1 0 15 1
0 C 0 1 1 0 15 1 0x4720646e 0x03020100 0x07060504 0x0b0a0908 0x0f0e0d0c 0x13121110 0x17161514 0x1b1a1918 0x1f1e1d1c 0x00000000 0x4a000000 0x00000000   X X X X X
# word 3
0 0 0 1 1 0 15 1 0x6c746e65 0x03020100 0x07060504 0x0b0a0908 0x0f0e0d0c 0x13121110 0x17161514 0x1b1a1918 0x1f1e1d1c 0x00000000 0x4a000000 0x00000000   0x81690ddd 1 0 15 1
0 C 0 1 1 0 15 1 0x6c746e65 0x03020100 0x07060504 0x0b0a0908 0x0f0e0d0c 0x13121110 0x17161514 0x1b1a1918 0x1f1e1d1c 0x00000000 0x4a000000 0x00000000   X X X X X
# word 4
0 0 0 1 1 0 15 1 0x6e656d65 0x03020100 0x07060504 0x0b0a0908 0x0f0e0d0c 0x13121110 0x17161514 0x1b1a1918 0x1f1e1d1c 0x00000000 0x4a000000 0x00000000   0xec7a7ee9 1 0 15 1
0 C 0 1 1 0 15 1 0x6e656d65 0x03020100 0x07060504 0x0b0a0908 0x0f0e0d0c 0x13121110 0x17161514 0x1b1a1918 0x1f1e1d1c 0x00000000 0x4a000000 0x00000000   X X X X X
# word 5
0 0 0 1 1 0 15 1 0x20666f20 0x03020100 0x07060504 0x0b0a0908 0x0f0e0d0c 0x13121110 0x17161514 0x1b1a1918 0x1f1e1d1c 0x00000000 0x4a000000 0x00000000   0xc260431d 1 0 15 1
0 C 0 1 1 0 15 1 0x20666f20 0x03020100 0x07060504 0x0b0a0908 0x0f0e0d0c 0x13121110 0x17161514 0x1b1a1918 0x1f1e1d1c 0x00000000 0x4a000000 0x00000000   X X X X X
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*/
